// Logisim project epu2.circ as structural Verilog: 8 circuits, main circuit main
module main (
);

  wire and_1_out, and_2_out, and_3_out, and_4_out, and_5_out, and_6_out, and_7_out, and_8_out,
       comparator_1_eq, comparator_2_eq, comparator_2_lt, cu_1_accwb, cu_1_aluen, cu_1_copy, cu_1_ctlstall,
       cu_1_ji, cu_1_jlz, cu_1_jnz, cu_1_jx, cu_1_jz, cu_1_ldi, cu_1_load, cu_1_memen, cu_1_memstall,
       cu_1_regwb, cu_1_save, cu_1_stall, cu_1_store, deex_1_accwbout, deex_1_aluenout, deex_1_copyout,
       deex_1_ctlstallout, deex_1_jiout, deex_1_jlzout, deex_1_jnzout, deex_1_jxout, deex_1_jzout,
       deex_1_ldiout, deex_1_loadout, deex_1_memstallout, deex_1_regwbout, deex_1_storeout, memory_1_ack,
       mmapDevices, mmapVram, multiplexer_3_out, not_1_out, or_1_out, or_2_out, or_3_out, or_4_out, or_5_out,
       or_6_out, or_7_out, register_4_q, register_7_q, sharedClk, sharedRst;
  wire [3:0] cu_1_opcode, cu_1_regnr, deex_1_opcodeout, deex_1_regnrout;
  wire [31:0] adder_1_out, adder_2_out, alu_1_c, controlled_buffer_1_out, controlled_buffer_5_out, cu_1_imm,
       deex_1_immout, memory_1_dataout, mmapAddr, mmapDataIn, mmapDataOut, multiplexer_1_out,
       multiplexer_2_out, regfile_1_readval, register_1_q, register_2_q, register_3_q, rom_1_data;

  assign controlled_buffer_1_out = not_1_out ? adder_1_out : 32'bz;  // Controlled_Buffer controlled_buffer_1
  Adder #(.width(32)) adder_1 (.a(register_1_q), .b(32'h1), .out(adder_1_out));  // open: cin, cout
  Adder #(.width(32)) adder_2 (.a(register_3_q), .b(deex_1_immout), .out(adder_2_out));  // open: cin, cout
  not not_1 (not_1_out, or_2_out);
  assign controlled_buffer_1_out = deex_1_jxout ? adder_2_out : 32'bz;  // Controlled_Buffer controlled_buffer_2
  assign controlled_buffer_1_out = or_5_out ? deex_1_immout : 32'bz;  // Controlled_Buffer controlled_buffer_3
  assign controlled_buffer_1_out = deex_1_jiout ? mmapDataIn : 32'bz;  // Controlled_Buffer controlled_buffer_4
  Register #(.width(32)) register_1 (
    .D(controlled_buffer_1_out), .en(or_1_out), .clk(sharedClk), .Q(register_1_q), .clr(sharedRst));
  or or_1 (or_1_out, or_3_out, or_2_out);
  or or_2 (or_2_out, deex_1_jxout, or_5_out, deex_1_jiout);
  ROM #(.addrWidth(24), .dataWidth(32)) rom_1 (.addr(register_1_q[23:0]), .data(rom_1_data));
  Register #(.width(32)) register_2 (.D(rom_1_data), .en(or_3_out), .clk(sharedClk), .Q(register_2_q), .clr(sharedRst));
  Register #(.width(32)) register_3 (
    .D(register_1_q), .en(or_3_out), .clk(sharedClk), .Q(register_3_q), .clr(sharedRst));
  and and_1 (and_1_out, multiplexer_3_out, ~cu_1_stall);  // AND_Gate
  and and_2 (and_2_out, multiplexer_3_out, register_4_q, cu_1_stall);
  or or_3 (or_3_out, and_1_out, and_2_out);
  CU cu_1 (
    .termIn(register_2_q), .stall(cu_1_stall), .memStall(cu_1_memstall), .ctlStall(cu_1_ctlstall),
    .accWb(cu_1_accwb), .regWb(cu_1_regwb), .memEn(cu_1_memen), .aluEn(cu_1_aluen), .ldi(cu_1_ldi),
    .load(cu_1_load), .store(cu_1_store), .copy(cu_1_copy), .save(cu_1_save), .jz(cu_1_jz), .jnz(cu_1_jnz),
    .jlz(cu_1_jlz), .opcode(cu_1_opcode), .regNr(cu_1_regnr), .imm(cu_1_imm), .jx(cu_1_jx), .ji(cu_1_ji));  // open: pcOW
  Clock clock_1 (.out(sharedClk));
  Register #(.width(1)) register_4 (.D(and_3_out), .clk(sharedClk), .Q(register_4_q), .clr(sharedRst));  // open: en
  and and_3 (and_3_out, cu_1_stall, ~and_2_out);  // AND_Gate
  Button button_1 (.out(sharedRst));
  Comparator #(.width(4)) comparator_1 (.a(cu_1_regnr), .b(deex_1_regnrout), .eq(comparator_1_eq));  // open: gt, lt
  // RGB_Video #(.cursor("No Cursor")) rgb_video_1: pin names not known; wires that end beside it: sharedRst, sharedClk, mmapVram, mmapAddr[13:7], mmapAddr[6:0], mmapDataIn[23:0]
  and and_4 (and_4_out, comparator_1_eq, deex_1_regwbout);
  regFile regfile_1 (
    .pc(register_3_q), .writeEna(deex_1_regwbout), .readNr(cu_1_regnr), .writeNr(deex_1_regnrout),
    .writeVal(mmapDataIn), .clk(sharedClk), .rst(sharedRst), .readVal(regfile_1_readval));
  Multiplexer #(.width(32)) multiplexer_1 (
    .in0(regfile_1_readval), .in1(mmapDataIn), .out(multiplexer_1_out), .sel(and_4_out));
  Register #(.width(32)) register_5 (
    .D(multiplexer_1_out), .en(multiplexer_3_out), .clk(sharedClk), .Q(mmapAddr), .clr(sharedRst));
  DEEX deex_1 (
    .memStallIn(cu_1_memstall), .ctlStallIn(cu_1_ctlstall), .accWbIn(cu_1_accwb), .regWbIn(cu_1_regwb),
    .memEnIn(cu_1_memen), .aluEnIn(cu_1_aluen), .ldiIn(cu_1_ldi), .loadIn(cu_1_load), .storeIn(cu_1_store),
    .copyIn(cu_1_copy), .saveIn(cu_1_save), .jzIn(cu_1_jz), .jnzIn(cu_1_jnz), .jlzIn(cu_1_jlz),
    .opcodeIn(cu_1_opcode), .regNrIn(cu_1_regnr), .immIn(cu_1_imm), .jxIn(cu_1_jx), .jiIn(cu_1_ji),
    .en(multiplexer_3_out), .clk(sharedClk), .rst(sharedRst), .memStallOut(deex_1_memstallout),
    .ctlStallOut(deex_1_ctlstallout), .accWbOut(deex_1_accwbout), .regWbOut(deex_1_regwbout),
    .aluEnOut(deex_1_aluenout), .ldiOut(deex_1_ldiout), .loadOut(deex_1_loadout), .storeOut(deex_1_storeout),
    .copyOut(deex_1_copyout), .jzOut(deex_1_jzout), .jnzOut(deex_1_jnzout), .jlzOut(deex_1_jlzout),
    .opcodeOut(deex_1_opcodeout), .regNrOut(deex_1_regnrout), .immOut(deex_1_immout), .jxOut(deex_1_jxout),
    .jiOut(deex_1_jiout));  // open: memEnOut, saveOut
  Multiplexer #(.width(32)) multiplexer_2 (
    .in0(mmapAddr), .in1(deex_1_immout), .out(multiplexer_2_out), .sel(deex_1_ldiout));
  memory memory_1 (
    .mmapData(mmapDataOut), .load(deex_1_loadout), .store(deex_1_storeout), .addr(mmapAddr),
    .dataIn(mmapDataIn), .clk(sharedClk), .mmapDevices(mmapDevices), .mmapVram(mmapVram), .ack(memory_1_ack),
    .dataOut(memory_1_dataout));
  alu alu_1 (.opSel(deex_1_opcodeout), .a(mmapDataIn), .b(mmapAddr), .c(alu_1_c));
  assign controlled_buffer_5_out = deex_1_loadout ? memory_1_dataout : 32'bz;  // Controlled_Buffer controlled_buffer_5
  assign controlled_buffer_5_out = deex_1_aluenout ? alu_1_c : 32'bz;  // Controlled_Buffer controlled_buffer_6
  assign controlled_buffer_5_out = or_4_out ? multiplexer_2_out : 32'bz;  // Controlled_Buffer controlled_buffer_7
  or or_4 (or_4_out, deex_1_ldiout, deex_1_copyout);
  Register #(.width(32)) register_6 (
    .D(controlled_buffer_5_out), .en(deex_1_accwbout), .clk(sharedClk), .Q(mmapDataIn), .clr(sharedRst));
  Comparator #(.width(32)) comparator_2 (
    .a(mmapDataIn), .b({32{1'b0}}), .eq(comparator_2_eq), .lt(comparator_2_lt));  // open: gt
  and and_5 (and_5_out, comparator_2_eq, deex_1_jzout);
  and and_6 (and_6_out, ~comparator_2_eq, deex_1_jnzout);  // AND_Gate
  and and_7 (and_7_out, comparator_2_lt, deex_1_jlzout);
  or or_5 (or_5_out, and_7_out, and_6_out, and_5_out);
  Multiplexer multiplexer_3 (.in0(1'b1), .in1(or_7_out), .out(multiplexer_3_out), .sel(or_6_out));
  or or_6 (or_6_out, deex_1_memstallout, deex_1_ctlstallout);
  and and_8 (and_8_out, memory_1_ack, deex_1_memstallout);
  or or_7 (or_7_out, and_8_out, register_7_q);
  Register #(.width(1)) register_7 (
    .D(deex_1_ctlstallout), .clk(sharedClk), .Q(register_7_q), .clr(sharedRst));  // open: en

  // Notes on the sheet:
  //   contents of rom_1 (hex, n*v repeats v):
  //   10000 113 67fd0000 513 220 203 141 213 503 fffb0008
endmodule

module CU (
  input  [31:0] termIn,
  output stall,
  output memStall,
  output ctlStall,
  output accWb,
  output regWb,
  output memEn,
  output aluEn,
  output ldi,
  output load,
  output store,
  output copy,
  output save,
  output jz,
  output jnz,
  output jlz,
  output [3:0] opcode,
  output [3:0] regNr,
  output [31:0] imm,
  output jx,
  output ji,
  output pcOW
);

  wire or_5_out, or_6_out;

  opDecode uOpDecode (
    .op(termIn[7:0]), .aluOp(aluEn), .ldiOp(ldi), .loadOp(load), .storeOp(store), .copyOp(copy),
    .saveOp(regWb), .jzOp(jz), .jnzOp(jnz), .jlzOp(jlz), .jxOp(jx), .jiOp(ji));
  assign imm = {{16{termIn[31]}}, termIn[31:16]};  // Bit_Extender bit_extender_1
  or or_1 (stall, memEn, ctlStall);
  or or_2 (memEn, load, store);
  or or_3 (ctlStall, pcOW, or_5_out);
  or or_4 (accWb, or_6_out, aluEn);
  or or_5 (or_5_out, jz, jnz, jlz);
  or or_6 (or_6_out, copy, ldi, load);
  or or_7 (pcOW, jx, ji);

  assign memStall = memEn;
  assign opcode = termIn[7:4];
  assign regNr = termIn[11:8];
  assign save = regWb;
endmodule

module opDecode (
  input  [7:0] op,
  output aluOp,
  output ldiOp,
  output loadOp,
  output storeOp,
  output copyOp,
  output saveOp,
  output jzOp,
  output jnzOp,
  output jlzOp,
  output jxOp,
  output jiOp
);

  wire jmp_out, mem_out, mov_out;

  nor mem (mem_out, op[0], op[3]);
  and mov (mov_out, op[0], op[1]);
  and jmp (jmp_out, ~op[0], op[3]);  // AND_Gate
  and alu (aluOp, op[0], ~op[1]);  // AND_Gate
  and ldi (ldiOp, mem_out, ~op[4], ~op[5]);  // AND_Gate
  and lod (loadOp, mem_out, op[4], ~op[5]);  // AND_Gate
  and str (storeOp, mem_out, ~op[4], op[5]);  // AND_Gate
  and cpy (copyOp, mov_out, ~op[4], ~op[5]);  // AND_Gate
  and sav (saveOp, mov_out, op[4], ~op[5]);  // AND_Gate
  and jz (jzOp, jmp_out, op[4], ~op[5], ~op[6]);  // AND_Gate
  and jnz (jnzOp, jmp_out, op[4], op[5], ~op[6]);  // AND_Gate
  and jlz (jlzOp, jmp_out, op[4], op[5], op[6]);
  and jx (jxOp, jmp_out, ~op[4], ~op[5]);  // AND_Gate
  and ji (jiOp, jmp_out, ~op[4], op[5]);  // AND_Gate
endmodule

module regFile (
  input  [31:0] pc,
  input  writeEna,
  input  [3:0] readNr,
  input  [3:0] writeNr,
  input  [31:0] writeVal,
  input  clk,
  input  rst,
  output [31:0] readVal
);

  wire decoder_1_out1, decoder_1_out2, decoder_1_out3, decoder_1_out4, decoder_1_out5, decoder_1_out6,
       decoder_1_out7, decoder_1_out8, decoder_1_out9, decoder_1_out10, decoder_1_out11, decoder_1_out12,
       decoder_1_out13, decoder_1_out14, decoder_1_out15;
  wire [31:0] register_1_q, register_2_q, register_3_q, register_4_q, register_5_q, register_6_q,
       register_7_q, register_8_q, register_9_q, register_10_q, register_11_q, register_12_q, register_13_q,
       register_14_q, register_15_q;

  Decoder #(.select(4)) decoder_1 (
    .out1(decoder_1_out1), .out2(decoder_1_out2), .out3(decoder_1_out3), .out4(decoder_1_out4),
    .out5(decoder_1_out5), .out6(decoder_1_out6), .out7(decoder_1_out7), .out8(decoder_1_out8),
    .out9(decoder_1_out9), .out10(decoder_1_out10), .out11(decoder_1_out11), .out12(decoder_1_out12),
    .out13(decoder_1_out13), .out14(decoder_1_out14), .out15(decoder_1_out15), .sel(writeNr), .en(writeEna));  // open: out0
  Register #(.width(32)) register_1 (.D(writeVal), .en(decoder_1_out1), .clk(clk), .Q(register_1_q), .clr(rst));
  Register #(.width(32)) register_2 (.D(writeVal), .en(decoder_1_out2), .clk(clk), .Q(register_2_q), .clr(rst));
  Register #(.width(32)) register_3 (.D(writeVal), .en(decoder_1_out3), .clk(clk), .Q(register_3_q), .clr(rst));
  Register #(.width(32)) register_4 (.D(writeVal), .en(decoder_1_out4), .clk(clk), .Q(register_4_q), .clr(rst));
  Register #(.width(32)) register_5 (.D(writeVal), .en(decoder_1_out5), .clk(clk), .Q(register_5_q), .clr(rst));
  Register #(.width(32)) register_6 (.D(writeVal), .en(decoder_1_out6), .clk(clk), .Q(register_6_q), .clr(rst));
  Register #(.width(32)) register_7 (.D(writeVal), .en(decoder_1_out7), .clk(clk), .Q(register_7_q), .clr(rst));
  Register #(.width(32)) register_8 (.D(writeVal), .en(decoder_1_out8), .clk(clk), .Q(register_8_q), .clr(rst));
  Register #(.width(32)) register_9 (.D(writeVal), .en(decoder_1_out9), .clk(clk), .Q(register_9_q), .clr(rst));
  Register #(.width(32)) register_10 (.D(writeVal), .en(decoder_1_out10), .clk(clk), .Q(register_10_q), .clr(rst));
  Register #(.width(32)) register_11 (.D(writeVal), .en(decoder_1_out11), .clk(clk), .Q(register_11_q), .clr(rst));
  Register #(.width(32)) register_12 (.D(writeVal), .en(decoder_1_out12), .clk(clk), .Q(register_12_q), .clr(rst));
  Register #(.width(32)) register_13 (.D(writeVal), .en(decoder_1_out13), .clk(clk), .Q(register_13_q), .clr(rst));
  Register #(.width(32)) register_14 (.D(writeVal), .en(decoder_1_out14), .clk(clk), .Q(register_14_q), .clr(rst));
  Register #(.width(32)) register_15 (.D(writeVal), .en(decoder_1_out15), .clk(clk), .Q(register_15_q), .clr(rst));
  Multiplexer #(.select(4), .width(32)) multiplexer_1 (
    .in0(pc), .in1(register_1_q), .in2(register_2_q), .in3(register_3_q), .in4(register_4_q),
    .in5(register_5_q), .in6(register_6_q), .in7(register_7_q), .in8(register_8_q), .in9(register_9_q),
    .in10(register_10_q), .in11(register_11_q), .in12(register_12_q), .in13(register_13_q),
    .in14(register_14_q), .in15(register_15_q), .out(readVal), .sel(readNr));
endmodule

module DEEX (
  input  memStallIn,
  input  ctlStallIn,
  input  accWbIn,
  input  regWbIn,
  input  memEnIn,
  input  aluEnIn,
  input  ldiIn,
  input  loadIn,
  input  storeIn,
  input  copyIn,
  input  saveIn,
  input  jzIn,
  input  jnzIn,
  input  jlzIn,
  input  [3:0] opcodeIn,
  input  [3:0] regNrIn,
  input  [31:0] immIn,
  input  jxIn,
  input  jiIn,
  input  en,
  input  clk,
  input  rst,
  output memStallOut,
  output ctlStallOut,
  output accWbOut,
  output regWbOut,
  output memEnOut,
  output aluEnOut,
  output ldiOut,
  output loadOut,
  output storeOut,
  output copyOut,
  output saveOut,
  output jzOut,
  output jnzOut,
  output jlzOut,
  output [3:0] opcodeOut,
  output [3:0] regNrOut,
  output [31:0] immOut,
  output jxOut,
  output jiOut
);

  Register #(.width(1)) register_1 (.D(memStallIn), .en(en), .clk(clk), .Q(memStallOut), .clr(rst));
  Register #(.width(1)) register_2 (.D(ctlStallIn), .en(en), .clk(clk), .Q(ctlStallOut), .clr(rst));
  Register #(.width(1)) register_3 (.D(accWbIn), .en(en), .clk(clk), .Q(accWbOut), .clr(rst));
  Register #(.width(1)) register_4 (.D(regWbIn), .en(en), .clk(clk), .Q(regWbOut), .clr(rst));
  Register #(.width(1)) register_5 (.D(memEnIn), .en(en), .clk(clk), .Q(memEnOut), .clr(rst));
  Register #(.width(1)) register_6 (.D(aluEnIn), .en(en), .clk(clk), .Q(aluEnOut), .clr(rst));
  Register #(.width(1)) register_7 (.D(ldiIn), .en(en), .clk(clk), .Q(ldiOut), .clr(rst));
  Register #(.width(1)) register_8 (.D(loadIn), .en(en), .clk(clk), .Q(loadOut), .clr(rst));
  Register #(.width(1)) register_9 (.D(storeIn), .en(en), .clk(clk), .Q(storeOut), .clr(rst));
  Register #(.width(1)) register_10 (.D(copyIn), .en(en), .clk(clk), .Q(copyOut), .clr(rst));
  Register #(.width(1)) register_11 (.D(saveIn), .en(en), .clk(clk), .Q(saveOut), .clr(rst));
  Register #(.width(1)) register_12 (.D(jzIn), .en(en), .clk(clk), .Q(jzOut), .clr(rst));
  Register #(.width(1)) register_13 (.D(jnzIn), .en(en), .clk(clk), .Q(jnzOut), .clr(rst));
  Register #(.width(1)) register_14 (.D(jlzIn), .en(en), .clk(clk), .Q(jlzOut), .clr(rst));
  Register #(.width(4)) register_15 (.D(opcodeIn), .en(en), .clk(clk), .Q(opcodeOut), .clr(rst));
  Register #(.width(4)) register_16 (.D(regNrIn), .en(en), .clk(clk), .Q(regNrOut), .clr(rst));
  Register #(.width(32)) register_17 (.D(immIn), .en(en), .clk(clk), .Q(immOut), .clr(rst));
  Register #(.width(1)) register_18 (.D(jxIn), .en(en), .clk(clk), .Q(jxOut), .clr(rst));
  Register #(.width(1)) register_19 (.D(jiIn), .en(en), .clk(clk), .Q(jiOut), .clr(rst));
endmodule

module alu (
  input  [3:0] opSel,
  input  [31:0] a,
  input  [31:0] b,
  output [31:0] c
);

  wire [15:0] divider_1_out, divider_1_rem;
  wire [31:0] adder_1_out, and_1_out, multiplier_1_out, not_1_out, or_1_out, shifter_1_out, shifter_2_out,
       subtractor_1_out, xor_1_out;

  assign and_1_out = a & b;  // AND_Gate and_1, 32 bits wide
  assign or_1_out = a | b;  // OR_Gate or_1, 32 bits wide
  assign not_1_out = ~a;  // NOT_Gate not_1, 32 bits wide
  assign xor_1_out = a ^ b;  // XOR_Gate xor_1, 32 bits wide
  Adder #(.width(32)) adder_1 (.a(a), .b(b), .out(adder_1_out));  // open: cin, cout
  Subtractor #(.width(32)) subtractor_1 (.a(a), .b(b), .out(subtractor_1_out));  // open: bin, bout
  Multiplier #(.width(32)) multiplier_1 (.a(a), .b(b), .out(multiplier_1_out));  // open: cin, cout
  Divider #(.width(16)) divider_1 (
    .a(a[15:0]), .b(b[15:0]), .out(divider_1_out), .upper(a[31:16]), .rem(divider_1_rem));
  Shifter #(.width(32)) shifter_1 (.in(a), .\dist (b[4:0]), .out(shifter_1_out));
  Shifter #(.shift("lr"), .width(32)) shifter_2 (.in(a), .\dist (b[4:0]), .out(shifter_2_out));
  Multiplexer #(.select(4), .width(32)) multiplexer_1 (
    .in0(and_1_out), .in1(or_1_out), .in2(not_1_out), .in3(xor_1_out), .in4(adder_1_out),
    .in5(subtractor_1_out), .in6(multiplier_1_out), .in7({divider_1_rem, divider_1_out}),
    .in8(shifter_1_out), .in9(shifter_2_out), .out(c), .sel(opSel));  // open: in10, in11, in12, in13, in14, in15
endmodule

module memory (
  input  [31:0] mmapData,
  input  load,
  input  store,
  input  [31:0] addr,
  input  [31:0] dataIn,
  input  clk,
  output mmapDevices,
  output mmapVram,
  output ack,
  output [31:0] dataOut
);

  wire comparator_1_gt, comparator_2_gt, or_2_out;
  wire [31:0] ram_1_dout;

  Comparator #(.mode("unsigned"), .width(32)) comparator_1 (
    .a(32'h4100), .b(addr), .gt(comparator_1_gt));  // open: eq, lt
  Comparator #(.mode("unsigned"), .width(32)) comparator_2 (
    .a(32'h4000), .b(addr), .gt(comparator_2_gt));  // open: eq, lt
  RAM #(.addrWidth(24), .dataWidth(32), .enables("line")) ram_1 (
    .addr(addr[23:0]), .we(store), .clk(clk), .din(dataIn), .dout(ram_1_dout));
  and and_1 (mmapDevices, comparator_1_gt, ~comparator_2_gt);  // AND_Gate
  or or_1 (ack, load, store);
  or or_2 (or_2_out, comparator_2_gt, mmapDevices);
  and and_2 (mmapVram, comparator_2_gt, store);
  Multiplexer #(.width(32)) multiplexer_1 (.in0(mmapData), .in1(ram_1_dout), .out(dataOut), .sel(or_2_out));
endmodule

module handshake (
  input  avlIn,
  input  thisAck,
  input  otherAck,
  input  clk,
  output avlOut,
  output ackOut
);

  wire register_2_q;

  Register #(.width(1)) register_1 (.D(avlIn), .en(ackOut), .clk(clk), .Q(avlOut));  // open: clr
  Register #(.width(1)) register_2 (.D(otherAck), .clk(clk), .Q(register_2_q));  // open: en, clr
  and and_1 (ackOut, thisAck, register_2_q);
endmodule
